// Logisim project BCD_Main.circ as structural Verilog: 1 circuit, main circuit main
module main (
  input  A,
  input  B,
  input  C,
  input  D
);

  wire bcd_a_1_a_2, bcd_b_1_b_2, bcd_c2_1_c_2, bcd_d_1_d_2, bcd_e_1_e, bcd_f_1_f, bcd_g_1_g;

  BCD_a bcd_a_1 (.A(A), .B(B), .C(C), .D(D), .a_2(bcd_a_1_a_2));
  BCD_b bcd_b_1 (.A(A), .B(B), .C(C), .D(D), .B_2(bcd_b_1_b_2));
  BCD_c2 bcd_c2_1 (.A(A), .B(B), .C(C), .D(D), .C_2(bcd_c2_1_c_2));
  BCD_d bcd_d_1 (.A(A), .B(B), .C(C), .D(D), .d_2(bcd_d_1_d_2));
  BCD_e bcd_e_1 (.A(A), .B(B), .C(C), .D(D), .e(bcd_e_1_e));
  BCD_f bcd_f_1 (.A(A), .B(B), .C(C), .D(D), .f(bcd_f_1_f));
  BCD_g bcd_g_1 (.A(A), .B(B), .C(C), .D(D), .g(bcd_g_1_g));
  _7_Segment_Display #(.active("false")) u_7_segment_display_1 (
    .g(bcd_g_1_g), .f(bcd_f_1_f), .a(bcd_a_1_a_2), .b(bcd_b_1_b_2), .e(bcd_e_1_e), .d(bcd_d_1_d_2),
    .c(bcd_c2_1_c_2));  // open: dp
endmodule
